// Digital circuit D flip flop falling.dig as structural Verilog
module D_flip_flop_falling (
  input  D,
  input  CLK,
  output Q
);

  wire multiplexer_1_out, not_1_out;

  Multiplexer multiplexer_1 (.sel(CLK), .in_0(multiplexer_1_out), .in_1(D), .out(multiplexer_1_out));
  Multiplexer multiplexer_2 (.sel(not_1_out), .in_0(Q), .in_1(multiplexer_1_out), .out(Q));
  not not_1 (not_1_out, CLK);
endmodule
