// Digital circuit D latch negative.dig as structural Verilog
module D_latch_negative (
  input  D,
  input  G,
  output Q_out
);

  wire not_1_out;

  Multiplexer multiplexer_1 (.sel(not_1_out), .in_0(Q_out), .in_1(D), .out(Q_out));
  not not_1 (not_1_out, G);
endmodule
