// Digital circuit D latch positive.dig as structural Verilog
module D_latch_positive (
  input  D,
  input  G,
  output Q_out
);

  Multiplexer multiplexer_1 (.sel(G), .in_0(Q_out), .in_1(D), .out(Q_out));
endmodule
