// Digital circuit Decoder (s=2).dig as structural Verilog
module Decoder__s_2 (
  input  S_2,
  input  S_1,
  output A_0,
  output A_1,
  output A_2,
  output A_3
);

  and and_1 (A_0, ~S_1, ~S_2);  // And
  and and_2 (A_1, S_1, ~S_2);  // And
  and and_3 (A_2, ~S_1, S_2);  // And
  and and_4 (A_3, S_1, S_2);
endmodule
