// Digital circuit Encoder (s=2).dig as structural Verilog
module Encoder__s_2 (
  input  A_3,
  input  A_2,
  input  A_4,
  input  A_1,
  output S_0,
  output S_1
);

  or or_1 (S_0, A_2, A_4);
  or or_2 (S_1, A_3, A_4);
endmodule
