// Digital circuit FA.dig as structural Verilog
module FA (
  input  A,
  input  B,
  input  C_in,
  output Sum,
  output C_out
);

  wire and_1_out, and_2_out, xor_1_out;

  and and_1 (and_1_out, B, A);
  or or_1 (C_out, and_2_out, and_1_out);
  and and_2 (and_2_out, xor_1_out, C_in);
  xor xor_1 (xor_1_out, B, A);
  xor xor_2 (Sum, xor_1_out, C_in);
endmodule
