// Digital circuit Inverter clock.dig as structural Verilog
module Inverter_clock (
);

  wire not_1_out, not_2_out, not_3_out, not_4_out, not_5_out, not_6_out, not_7_out, not_8_out, not_9_out;

  not not_1 (not_1_out, not_9_out);
  not not_2 (not_2_out, not_1_out);
  not not_3 (not_3_out, not_2_out);
  not not_4 (not_4_out, not_3_out);
  not not_5 (not_5_out, not_4_out);
  not not_6 (not_6_out, not_5_out);
  not not_7 (not_7_out, not_6_out);
  not not_8 (not_8_out, not_7_out);
  not not_9 (not_9_out, not_8_out);

  // Notes on the sheet:
  //   Note: When running this circuit, you will get an error
  //   "Logic seems to oscillate"
  //   Which, of course, is what we intend with this clock design lol
endmodule
