// Digital circuit MUX(s=1).dig as structural Verilog
module MUX_s_1 (
  input  S,
  input  A,
  input  B,
  output Y
);

  wire and_1_out, and_2_out;

  and and_1 (and_1_out, A, ~S);  // And
  and and_2 (and_2_out, B, S);
  or or_1 (Y, and_1_out, and_2_out);
endmodule
