// Digital circuit Adder-subtractor-4-bit.dig as structural Verilog
module Adder_subtractor_4_bit (
  input  A_3,
  input  A_2,
  input  A_1,
  input  A_0,
  input  B_3,
  input  B_2,
  input  B_1,
  input  B_0,
  input  Sub,
  output S_3,
  output S_2,
  output S_1,
  output S_0,
  output FlagZ,
  output FlagC
);

  wire add_2_c_o, add_3_c_o, add_4_c_o, B_0_t, B_1_t, B_2_t, B_3_t;

  Add add_1 (.a(A_3), .b(B_3_t), .c_i(add_2_c_o), .s(S_3), .c_o(FlagC));
  Add add_2 (.a(A_2), .b(B_2_t), .c_i(add_3_c_o), .s(S_2), .c_o(add_2_c_o));
  xor xor_1 (B_3_t, Sub, B_3);
  Add add_3 (.a(A_1), .b(B_1_t), .c_i(add_4_c_o), .s(S_1), .c_o(add_3_c_o));
  xor xor_2 (B_2_t, Sub, B_2);
  nor nor_1 (FlagZ, S_0, S_1, S_2, S_3);
  xor xor_3 (B_1_t, Sub, B_1);
  Add add_4 (.a(A_0), .b(B_0_t), .c_i(Sub), .s(S_0), .c_o(add_4_c_o));
  xor xor_4 (B_0_t, Sub, B_0);

  // Other names for the same wires on the sheet: MSB_Carry_Out = FlagC

  // Notes on the sheet:
  //   FlagC
  //   FlagZ = big NOR(Sum bits)
  //   If all Sum bits are 0
  //   then FlagZ=1
endmodule
